// Logisim project fULL ADDER AND HALF ADDER.circ as structural Verilog: 1 circuit, main circuit main
module main (
  input  A,
  input  B,
  input  A_2,
  input  A_3,
  input  B_2,
  input  B_3,
  input  C,
  input  C_2,
  output S,
  output C_3,
  output S_2,
  output S_3,
  output C1,
  output C1_2
);

  wire and_2_out, and_3_out, xor_2_out;

  xor xor_1 (S, A, B);
  and and_1 (C_3, A, B);
  xor xor_2 (xor_2_out, A_2, B_3);
  and and_2 (and_2_out, A_2, B_3);
  and and_3 (and_3_out, xor_2_out, C_2);
  xor xor_3 (S_2, xor_2_out, C_2);
  or or_1 (C1_2, and_3_out, and_2_out);
  Adder #(.width(1)) adder_1 (.a(B_2), .b(C), .out(S_3), .cin(A_3), .cout(C1));

  // Notes on the sheet:
  //   Half Adder
  //   Full Adder
  //   C1= ( A XOR B ).C+A.B
endmodule
